# Fritzing sketch Montaggio IR (saved by Fritzing 0.9.3b)
breadboards: 1

parts:
  Componente1 = Arduino Uno (Rev3)
  LED1 = LED - 5mm [color="Infrared (940nm)" package="5 mm [THT]"]
  LED2 = LED - 5mm [color="Infrared (940nm)" package="5 mm [THT]"]
  R1 = Resistor [tolerance=±5% resistance=270 package=THT]
  R2 = Resistor [tolerance=±5% resistance=10k package=THT]

nets:
  N1: Componente1.D5_PWM, R1.Pin_0
  N2: Componente1.D6_PWM, LED2.anode, R2.Pin_0
  N3: Componente1.5V, R2.Pin_1
  N4: Componente1.GND, LED1.cathode, LED2.cathode
  N5: LED1.anode, R1.Pin_1

notes:
  R1
  R2
  IR DETECTOR
  IR EMITTER
  R1: 10 kOhm
  R2 : 270 Ohm
